// Logisim project Issifu_01111110_IC.circ as structural Verilog: 4 circuits, main circuit main
module main (
);

  wire AND_p3, clock_out, Frame_marker_detector_y, JK_p4, n7segdisp_1_a, n7segdisp_1_b, n7segdisp_1_c,
       n7segdisp_1_d, n7segdisp_1_e, n7segdisp_1_f, n7segdisp_1_g, n7segdisp_2_a, n7segdisp_2_b,
       n7segdisp_2_c, n7segdisp_2_d, n7segdisp_2_e, n7segdisp_2_f, n7segdisp_2_g, n7segdisp_3_a,
       n7segdisp_3_b, n7segdisp_3_c, n7segdisp_3_d, n7segdisp_3_e, n7segdisp_3_f, n7segdisp_3_g,
       n7segdisp_4_a, n7segdisp_4_b, n7segdisp_4_c, n7segdisp_4_d, n7segdisp_4_e, n7segdisp_4_f,
       n7segdisp_4_g, oto9_1_q0, oto9_1_q1, oto9_1_q2, oto9_1_q3, oto9_2_q0, oto9_2_q1, oto9_2_q2, oto9_2_q3,
       oto9_2_when0, oto9_3_q0, oto9_3_q1, oto9_3_q2, oto9_3_q3, oto9_4_q0, oto9_4_q1, oto9_4_q2, oto9_4_q3,
       oto9_4_when0, rom_1_data;
  wire [7:0] counter_1_q;

  Clock clock (.out(clock_out));
  Counter counter_1 (.Q(counter_1_q), .clk(clock_out));  // open: load, D, count, carry, clr
  ROM #(.dataWidth(1)) rom_1 (.addr(counter_1_q), .data(rom_1_data));  // open: sel
  detector01111110 Frame_marker_detector (.X(rom_1_data), .CLK(clock_out), .Y(Frame_marker_detector_y));
  LED frame_marker_detected (.in(Frame_marker_detector_y));
  // _7476 JK: pin names not known; wires that end beside it: clock_out, Frame_marker_detector_y, Frame_marker_detector_y, JK_p4
  // _7408 AND: pin names not known; wires that end beside it: JK_p4, clock_out, AND_p3
  _7_Segment_Display u_7_segment_display_1 (
    .g(n7segdisp_1_g), .f(n7segdisp_1_f), .a(n7segdisp_1_a), .b(n7segdisp_1_b), .e(n7segdisp_1_e),
    .d(n7segdisp_1_d), .c(n7segdisp_1_c));  // open: dp
  Oto9 oto9_1 (
    .RST(Frame_marker_detector_y), .CLK(oto9_2_when0), .Q0(oto9_1_q0), .Q1(oto9_1_q1), .Q2(oto9_1_q2),
    .Q3(oto9_1_q3));  // open: when0
  _7segDisp u_7segdisp_1 (
    .Q3(oto9_1_q3), .Q2(oto9_1_q2), .Q1(oto9_1_q1), .Q0(oto9_1_q0), .a(n7segdisp_1_a), .b(n7segdisp_1_b),
    .c(n7segdisp_1_c), .d(n7segdisp_1_d), .e(n7segdisp_1_e), .f(n7segdisp_1_f), .g(n7segdisp_1_g));
  Oto9 oto9_2 (
    .RST(Frame_marker_detector_y), .CLK(AND_p3), .Q0(oto9_2_q0), .Q1(oto9_2_q1), .Q2(oto9_2_q2),
    .Q3(oto9_2_q3), .when0(oto9_2_when0));
  _7segDisp u_7segdisp_2 (
    .Q3(oto9_2_q3), .Q2(oto9_2_q2), .Q1(oto9_2_q1), .Q0(oto9_2_q0), .a(n7segdisp_2_a), .b(n7segdisp_2_b),
    .c(n7segdisp_2_c), .d(n7segdisp_2_d), .e(n7segdisp_2_e), .f(n7segdisp_2_f), .g(n7segdisp_2_g));
  _7_Segment_Display u_7_segment_display_2 (
    .g(n7segdisp_2_g), .f(n7segdisp_2_f), .a(n7segdisp_2_a), .b(n7segdisp_2_b), .e(n7segdisp_2_e),
    .d(n7segdisp_2_d), .c(n7segdisp_2_c));  // open: dp
  Oto9 oto9_3 (.CLK(oto9_4_when0), .Q0(oto9_3_q0), .Q1(oto9_3_q1), .Q2(oto9_3_q2), .Q3(oto9_3_q3));  // open: RST, when0
  _7segDisp u_7segdisp_3 (
    .Q3(oto9_3_q3), .Q2(oto9_3_q2), .Q1(oto9_3_q1), .Q0(oto9_3_q0), .a(n7segdisp_3_a), .b(n7segdisp_3_b),
    .c(n7segdisp_3_c), .d(n7segdisp_3_d), .e(n7segdisp_3_e), .f(n7segdisp_3_f), .g(n7segdisp_3_g));
  _7_Segment_Display u_7_segment_display_3 (
    .g(n7segdisp_3_g), .f(n7segdisp_3_f), .a(n7segdisp_3_a), .b(n7segdisp_3_b), .e(n7segdisp_3_e),
    .d(n7segdisp_3_d), .c(n7segdisp_3_c));  // open: dp
  Oto9 oto9_4 (
    .CLK(Frame_marker_detector_y), .Q0(oto9_4_q0), .Q1(oto9_4_q1), .Q2(oto9_4_q2), .Q3(oto9_4_q3),
    .when0(oto9_4_when0));  // open: RST
  _7segDisp u_7segdisp_4 (
    .Q3(oto9_4_q3), .Q2(oto9_4_q2), .Q1(oto9_4_q1), .Q0(oto9_4_q0), .a(n7segdisp_4_a), .b(n7segdisp_4_b),
    .c(n7segdisp_4_c), .d(n7segdisp_4_d), .e(n7segdisp_4_e), .f(n7segdisp_4_f), .g(n7segdisp_4_g));
  _7_Segment_Display u_7_segment_display_4 (
    .g(n7segdisp_4_g), .f(n7segdisp_4_f), .a(n7segdisp_4_a), .b(n7segdisp_4_b), .e(n7segdisp_4_e),
    .d(n7segdisp_4_d), .c(n7segdisp_4_c));  // open: dp

  // Notes on the sheet:
  //   bit stream
  //   ALHASSAN ISSIFU - 52222021
  //   contents of rom_1 (hex, n*v repeats v):
  //   4*1 5*0 6*1 0 1 1 1 0 0 1 0 1 0 0 1 0 1 0 0 1 0 0 5*1 0 6*1 0 1 1 0 6*1 0 0 5*1 0 0 6*1 0 6*1 0 0
  //   6*1 0 0 1 1 1 0 0 1 1 0 6*1 5*0 6*1 0 0 0 1 0 0 1 1 0 0 1 0 1 0 1 0 0 5*1 0 1 0 0 6*1 0 1 0 0 11*1 0
  //   6*1 0 0 0 1 1 1 0 1 1 0 0 6*1 0 1 1 1 0 0 1 1 0 6*1 0 0 6*1 0 1 0 6*1 4*0 6*1 0 0 0 1 1 0 0 1 0 1 0
  //   0 1 0 1 1 0 1 0 1 0 1 0 6*1
  //   Number of bits detected
  //   Number of frame markers detected
endmodule

module detector01111110 (
  input  X,
  input  CLK,
  output Y
);

  wire AND_p6, AND_p9, AND_p12, JK_2_p3, NAND_p3, OR_p1, OR_p2, OR_p3, OR_p6, OR_p7, OR_p9, OR_p11, OR_p12;

  // _7400 NAND: pin names not known; wires that end beside it: X, X, NAND_p3
  // _7432 OR: pin names not known; wires that end beside it: OR_p1, OR_p2, OR_p3, OR_p3, NAND_p3, OR_p6, OR_p7, X, OR_p9, NAND_p3, OR_p11, OR_p12
  // _7408 AND: pin names not known; wires that end beside it: OR_p1, OR_p2, OR_p7, OR_p11, OR_p1, AND_p6, X, OR_p11, AND_p9, AND_p9, OR_p1, AND_p12
  // _7476 JK: pin names not known; wires that end beside it: CLK, OR_p6, CLK, OR_p9, OR_p11, OR_p12, OR_p1, AND_p9
  // _7476 JK_2: pin names not known; wires that end beside it: CLK, AND_p12, JK_2_p3, OR_p2
  // _7432 OR_2: pin names not known; wires that end beside it: AND_p6, NAND_p3, JK_2_p3
  // _7421 7421_1: pin names not known; wires that end beside it: OR_p2, NAND_p3, OR_p1, OR_p11, Y
endmodule

module Oto9 (
  input  RST,
  input  CLK,
  output Q0,
  output Q1,
  output Q2,
  output Q3,
  output when0
);

  wire n7408_1_p2, n7408_1_p3, n7408_1_p6, n7408_1_p11, n7408_1_p14, n7432_1_p3, n7476_1_p9, n7476_1_p13,
       n7476_2_p9;

  // _7408 7408_1: pin names not known; wires that end beside it: Q0, n7408_1_p2, n7408_1_p3, Q1, Q0, n7408_1_p6, 1'b0, 1'b1, Q0, Q3, n7408_1_p11, n7408_1_p6, Q2, n7408_1_p14
  // _7476 7476_1: pin names not known; wires that end beside it: CLK, RST, 1'b1, 1'b1, CLK, RST, 1'b1, Q0, n7476_1_p9, 1'b0, n7408_1_p3, Q1, n7476_1_p13, n7408_1_p3
  // _7432 7432_1: pin names not known; wires that end beside it: n7408_1_p14, n7408_1_p11, n7432_1_p3, 1'b0, 1'b1
  // _7476 7476_2: pin names not known; wires that end beside it: CLK, RST, n7408_1_p6, 1'b1, CLK, RST, n7408_1_p6, Q2, n7476_2_p9, 1'b0, n7432_1_p3, Q3, n7408_1_p2, n7432_1_p3
  // _7421 7421_1: pin names not known; wires that end beside it: n7408_1_p2, n7476_2_p9, n7476_1_p13, n7476_1_p9, when0

  // Notes on the sheet:
  //   AND
  //   JK
  //   OR
  //   JK
endmodule

module _7segDisp (
  input  Q3,
  input  Q2,
  input  Q1,
  input  Q0,
  output a,
  output b,
  output c,
  output d,
  output e,
  output f,
  output g
);

  // _7448 7448_1: pin names not known; wires that end beside it: Q1, Q2, 1'b1, 1'b1, Q3, Q0, 1'b1, f, g, a, b, c, d, e
endmodule
