// Logisim project Issifu_01111110_Gates.circ as structural Verilog: 4 circuits, main circuit main
module main (
);

  wire and_1_out, clock_out, Frame_marker_detector_y, j_k_ff_1_q, n7segdisp_1_a, n7segdisp_1_b,
       n7segdisp_1_c, n7segdisp_1_d, n7segdisp_1_e, n7segdisp_1_f, n7segdisp_1_g, n7segdisp_2_a,
       n7segdisp_2_b, n7segdisp_2_c, n7segdisp_2_d, n7segdisp_2_e, n7segdisp_2_f, n7segdisp_2_g,
       n7segdisp_3_a, n7segdisp_3_b, n7segdisp_3_c, n7segdisp_3_d, n7segdisp_3_e, n7segdisp_3_f,
       n7segdisp_3_g, n7segdisp_4_a, n7segdisp_4_b, n7segdisp_4_c, n7segdisp_4_d, n7segdisp_4_e,
       n7segdisp_4_f, n7segdisp_4_g, oto9_1_q0, oto9_1_q1, oto9_1_q2, oto9_1_q3, oto9_2_q0, oto9_2_q1,
       oto9_2_q2, oto9_2_q3, oto9_2_when0, oto9_3_q0, oto9_3_q1, oto9_3_q2, oto9_3_q3, oto9_4_q0, oto9_4_q1,
       oto9_4_q2, oto9_4_q3, oto9_4_when0, rom_1_data;
  wire [7:0] counter_1_q;

  Clock clock (.out(clock_out));
  Counter counter_1 (.Q(counter_1_q), .clk(clock_out));  // open: load, D, count, carry, clr
  ROM #(.dataWidth(1)) rom_1 (.addr(counter_1_q), .data(rom_1_data));  // open: sel
  detector01111110 Frame_marker_detector (.X(rom_1_data), .CLK(clock_out), .Y(Frame_marker_detector_y));
  LED frame_marker_detected (.in(Frame_marker_detector_y));
  J_K_Flip_Flop j_k_ff_1 (
    .J(Frame_marker_detector_y), .clk(clock_out), .K(Frame_marker_detector_y), .Q(j_k_ff_1_q));  // open: Qn, preset, en, reset
  and and_1 (and_1_out, j_k_ff_1_q, clock_out);
  _7_Segment_Display u_7_segment_display_1 (
    .g(n7segdisp_1_g), .f(n7segdisp_1_f), .a(n7segdisp_1_a), .b(n7segdisp_1_b), .e(n7segdisp_1_e),
    .d(n7segdisp_1_d), .c(n7segdisp_1_c));  // open: dp
  Oto9 oto9_1 (
    .RST(Frame_marker_detector_y), .CLK(oto9_2_when0), .Q0(oto9_1_q0), .Q1(oto9_1_q1), .Q2(oto9_1_q2),
    .Q3(oto9_1_q3));  // open: when0
  _7segDisp u_7segdisp_1 (
    .Q3(oto9_1_q3), .Q2(oto9_1_q2), .Q1(oto9_1_q1), .Q0(oto9_1_q0), .a(n7segdisp_1_a), .b(n7segdisp_1_b),
    .c(n7segdisp_1_c), .d(n7segdisp_1_d), .e(n7segdisp_1_e), .f(n7segdisp_1_f), .g(n7segdisp_1_g));
  Oto9 oto9_2 (
    .RST(Frame_marker_detector_y), .CLK(and_1_out), .Q0(oto9_2_q0), .Q1(oto9_2_q1), .Q2(oto9_2_q2),
    .Q3(oto9_2_q3), .when0(oto9_2_when0));
  _7segDisp u_7segdisp_2 (
    .Q3(oto9_2_q3), .Q2(oto9_2_q2), .Q1(oto9_2_q1), .Q0(oto9_2_q0), .a(n7segdisp_2_a), .b(n7segdisp_2_b),
    .c(n7segdisp_2_c), .d(n7segdisp_2_d), .e(n7segdisp_2_e), .f(n7segdisp_2_f), .g(n7segdisp_2_g));
  _7_Segment_Display u_7_segment_display_2 (
    .g(n7segdisp_2_g), .f(n7segdisp_2_f), .a(n7segdisp_2_a), .b(n7segdisp_2_b), .e(n7segdisp_2_e),
    .d(n7segdisp_2_d), .c(n7segdisp_2_c));  // open: dp
  Oto9 oto9_3 (.CLK(oto9_4_when0), .Q0(oto9_3_q0), .Q1(oto9_3_q1), .Q2(oto9_3_q2), .Q3(oto9_3_q3));  // open: RST, when0
  _7segDisp u_7segdisp_3 (
    .Q3(oto9_3_q3), .Q2(oto9_3_q2), .Q1(oto9_3_q1), .Q0(oto9_3_q0), .a(n7segdisp_3_a), .b(n7segdisp_3_b),
    .c(n7segdisp_3_c), .d(n7segdisp_3_d), .e(n7segdisp_3_e), .f(n7segdisp_3_f), .g(n7segdisp_3_g));
  _7_Segment_Display u_7_segment_display_3 (
    .g(n7segdisp_3_g), .f(n7segdisp_3_f), .a(n7segdisp_3_a), .b(n7segdisp_3_b), .e(n7segdisp_3_e),
    .d(n7segdisp_3_d), .c(n7segdisp_3_c));  // open: dp
  Oto9 oto9_4 (
    .CLK(Frame_marker_detector_y), .Q0(oto9_4_q0), .Q1(oto9_4_q1), .Q2(oto9_4_q2), .Q3(oto9_4_q3),
    .when0(oto9_4_when0));  // open: RST
  _7segDisp u_7segdisp_4 (
    .Q3(oto9_4_q3), .Q2(oto9_4_q2), .Q1(oto9_4_q1), .Q0(oto9_4_q0), .a(n7segdisp_4_a), .b(n7segdisp_4_b),
    .c(n7segdisp_4_c), .d(n7segdisp_4_d), .e(n7segdisp_4_e), .f(n7segdisp_4_f), .g(n7segdisp_4_g));
  _7_Segment_Display u_7_segment_display_4 (
    .g(n7segdisp_4_g), .f(n7segdisp_4_f), .a(n7segdisp_4_a), .b(n7segdisp_4_b), .e(n7segdisp_4_e),
    .d(n7segdisp_4_d), .c(n7segdisp_4_c));  // open: dp

  // Notes on the sheet:
  //   bit stream
  //   ALHASSAN ISSIFU - 52222021
  //   contents of rom_1 (hex, n*v repeats v):
  //   4*1 5*0 6*1 0 1 1 1 0 0 1 0 1 0 0 1 0 1 0 0 1 0 0 5*1 0 6*1 0 1 1 0 6*1 0 0 5*1 0 0 6*1 0 6*1 0 0
  //   6*1 0 0 1 1 1 0 0 1 1 0 6*1 5*0 6*1 0 0 0 1 0 0 1 1 0 0 1 0 1 0 1 0 0 5*1 0 1 0 0 6*1 0 1 0 0 11*1 0
  //   6*1 0 0 0 1 1 1 0 1 1 0 0 6*1 0 1 1 1 0 0 1 1 0 6*1 0 0 6*1 0 1 0 6*1 4*0 6*1 0 0 0 1 1 0 0 1 0 1 0
  //   0 1 0 1 1 0 1 0 1 0 1 0 6*1
  //   Number of bits detected
  //   Number of frame markers detected
endmodule

module detector01111110 (
  input  X,
  input  CLK,
  output Y
);

  wire and_1_out, and_2_out, and_3_out, and_4_out, not_1_out, or_1_out, or_2_out, or_3_out, or_4_out;
  wire [2:0] j_k_ff_1_q;

  not not_1 (not_1_out, X);
  and and_1 (and_1_out, j_k_ff_1_q[1], j_k_ff_1_q[2]);
  or or_1 (or_1_out, j_k_ff_1_q[1], j_k_ff_1_q[2], not_1_out);
  or or_2 (or_2_out, X, and_1_out);
  J_K_Flip_Flop j_k_ff_1 (.J(or_1_out), .clk(CLK), .K(or_2_out), .Q(j_k_ff_1_q[0]));  // open: Qn, preset, en, reset
  Hex_Digit_Display hex_digit_display_1 (.value({1'b0, j_k_ff_1_q}));  // open: dp
  and and_2 (and_2_out, j_k_ff_1_q[0], X);
  or or_3 (or_3_out, j_k_ff_1_q[0], not_1_out);
  J_K_Flip_Flop j_k_ff_2 (.J(and_2_out), .clk(CLK), .K(or_3_out), .Q(j_k_ff_1_q[1]));  // open: Qn, preset, en, reset
  and and_3 (and_3_out, j_k_ff_1_q[1], j_k_ff_1_q[0]);
  or or_4 (or_4_out, and_3_out, not_1_out);
  and and_4 (and_4_out, and_2_out, j_k_ff_1_q[1]);
  J_K_Flip_Flop j_k_ff_3 (.J(and_4_out), .clk(CLK), .K(or_4_out), .Q(j_k_ff_1_q[2]));  // open: Qn, preset, en, reset
  and and_5 (Y, not_1_out, j_k_ff_1_q[0], j_k_ff_1_q[1], j_k_ff_1_q[2]);
  LED u_Y (.in(Y));

  // Notes on the sheet:
  //   S
endmodule

module Oto9 (
  input  RST,
  input  CLK,
  output Q1,
  output Q2,
  output Q0,
  output Q3,
  output when0
);

  wire and_1_out, and_2_out, and_3_out, and_4_out, j_k_ff_1_qn, j_k_ff_2_qn, j_k_ff_3_qn, j_k_ff_4_qn,
       or_1_out;

  J_K_Flip_Flop j_k_ff_1 (.J(1'b1), .clk(CLK), .K(1'b1), .Q(Q0), .Qn(j_k_ff_1_qn), .reset(RST));  // open: preset, en
  and and_1 (and_1_out, Q0, j_k_ff_4_qn);
  J_K_Flip_Flop j_k_ff_2 (
    .J(and_1_out), .clk(CLK), .K(and_1_out), .Q(Q1), .Qn(j_k_ff_2_qn), .reset(RST));  // open: preset, en
  and and_2 (and_2_out, Q0, Q1);
  J_K_Flip_Flop j_k_ff_3 (
    .J(and_2_out), .clk(CLK), .K(and_2_out), .Q(Q2), .Qn(j_k_ff_3_qn), .reset(RST));  // open: preset, en
  and and_3 (and_3_out, Q3, Q0);
  and and_4 (and_4_out, Q2, and_2_out);
  or or_1 (or_1_out, and_3_out, and_4_out);
  J_K_Flip_Flop j_k_ff_4 (
    .J(or_1_out), .clk(CLK), .K(or_1_out), .Q(Q3), .Qn(j_k_ff_4_qn), .reset(RST));  // open: preset, en
  and and_5 (when0, j_k_ff_1_qn, j_k_ff_2_qn, j_k_ff_3_qn, j_k_ff_4_qn);
endmodule

module _7segDisp (
  input  Q3,
  input  Q2,
  input  Q1,
  input  Q0,
  output a,
  output b,
  output c,
  output d,
  output e,
  output f,
  output g
);

  wire and_1_out, and_2_out, and_3_out, and_4_out, and_5_out, and_6_out, and_7_out, and_8_out, and_9_out,
       not_1_out, not_2_out, not_3_out;

  not not_1 (not_1_out, Q2);
  not not_2 (not_2_out, Q1);
  not not_3 (not_3_out, Q0);
  and and_1 (and_1_out, Q2, not_2_out);
  and and_2 (and_2_out, Q2, not_3_out);
  and and_3 (and_3_out, Q2, Q0);
  and and_4 (and_4_out, not_1_out, not_3_out);
  and and_5 (and_5_out, Q1, Q0);
  and and_6 (and_6_out, not_2_out, not_3_out);
  or or_1 (c, Q2, not_2_out, Q0);
  and and_7 (and_7_out, Q1, not_3_out);
  and and_8 (and_8_out, not_1_out, Q1);
  and and_9 (and_9_out, Q0, and_1_out);
  or or_2 (a, and_3_out, and_4_out, Q3, Q1);
  or or_3 (b, and_5_out, and_6_out, not_1_out);
  or or_4 (d, Q3, and_7_out, and_8_out, and_4_out, and_9_out);
  or or_5 (e, and_4_out, and_7_out);
  or or_6 (f, and_6_out, and_1_out, and_2_out, Q3);
  or or_7 (g, and_8_out, and_7_out, and_1_out, Q3);
endmodule
